# Fritzing sketch pump-controllers (saved by Fritzing 0.9.3b)

parts:
  Part1 = Arduino Uno (Rev3)
  U2 = G3VM-61E1 [package=g3vm-61e1]
  D1 = SOLAR-IXYS [package=solarbit-12x1]
  D2 = Diode [package=diode-1n4001]
  Part2 = PowerBoost 500 Charger  # not connected
  BAT2 = Battery Holders [package=battery-aa]  # not connected
  Part3 = Power Cell LiPo Charger/Booster  # not connected
  U3 = Vibration Motor- ROB-08449 [package=vibe-motor-10mm]
  R1 = Rotary Potentiometer (Large) [maximum_resistance=100kΩ package=THT]
  U4 = Vibration Motor- ROB-08449 [package=vibe-motor-10mm]  # not connected

nets:
  N1: Part1.D13/SCK, U2.SIG
  5V: Part1.5V, U2.VCC
  GND: Part1.GND, U2.GND
  N2: U2.C, R1.leg2
  N3: U2.NO, U3.-
  N4: D1.A, D2.C
  N5: U3.+, R1.leg1

custom parts:
  G3VM-61E1: Omron NO solid state relay

// code stored in the sketch: board-controller.ino
#include <ESP8266WiFi.h>
#include <secrets.h>

void setup() {
	Serial.begin(115200);
	delay(10);
	Serial.print("\n");
	WiFi.begin(GARDEN_SSID, GARDEN_PASSWORD);
	Serial.print("Connecting to ");
	Serial.print(GARDEN_SSID);
	Serial.print('\n');
	
	int i = 0;
	while(WiFi.status() != WL_CONNECTED) {
		delay(1000);
		Serial.print("Attempting connection number ");
		Serial.print(++i);
		Serial.print('\n');
	}

	Serial.print('\n');
	Serial.print("Connection Successful!");
	Serial.print('\n');
	Serial.print("IP Address: ");
	Serial.print(WiFi.localIP());
}

// code stored in the sketch: secrets.ino
#ifndef SECRETS_H
#define SECRETS_H

const char* GARDEN_SSID = "CoolPeopleFortNoLosersAllowed";
const char* GARDEN_PASSWORD = "blueberrybutthole29";

#endif
